// Logisim project projeto (1).circ as structural Verilog: 8 circuits, main circuit main
module main (
  input  in_1
);

  wire ALUSrc, ALUZero, CLK, MemRead, MemToReg, MemWrite, RegWrite;
  wire [2:0] funct3, ImmSel;
  wire [3:0] ALUOP, ALUOp_t;
  wire [4:0] rd, rs1, rs2;
  wire [6:0] funct7, opcode;
  wire [7:0] instructionf_1_currentpc, NextPC, PC4;
  wire [11:0] B_Imm, I_Imm, S_Imm;
  wire [19:0] J_Imm, U_Imm;
  wire [31:0] ALU_Data, data, Imm, instructionf_1_instrucao, MemData, rd1, rd2, RegData;

  Clock clock_1 (.out(CLK));
  // Probe on instructionf_1_currentpc
  InstructionF instructionf_1 (
    .CLK(CLK), .RST(in_1), .NextPC(NextPC), .CurrentPC(instructionf_1_currentpc),
    .Instrucao(instructionf_1_instrucao));
  Adder adder_1 (.a(8'h4), .b(instructionf_1_currentpc), .out(PC4));  // open: cin, cout
  // Probe on PC4
  IntructionD intructiond_1 (
    .Instrucao(instructionf_1_instrucao), .opcode(opcode), .rd(rd), .funct3(funct3), .rs1(rs1), .rs2(rs2),
    .funct7(funct7), .I_Imm(I_Imm), .S_Imm(S_Imm), .B_Imm(B_Imm), .U_Imm(U_Imm), .J_Imm(J_Imm));
  // Probe on rd1
  BR br_1 (
    .CLK(CLK), .RST(in_1), .RegWrite(RegWrite), .RS1(rs1), .RS2(rs2), .RD(rd), .Data(RegData), .RD1(rd1),
    .RD2(rd2));
  ImmGen immgen_1 (
    .ImmSel(ImmSel), .I_imm(I_Imm), .S_imm(S_Imm), .B_imm(B_Imm), .U_imm(U_Imm), .J_imm(J_Imm), .Imediato(Imm));
  UC uc_1 (
    .opcode(opcode), .funct3(funct3), .funct7(funct7), .CLK(CLK), .ImmSel(ImmSel), .RegWrite(RegWrite),
    .ALUSrc(ALUSrc), .ALUOp(ALUOp_t), .MemRead(MemRead), .MemToRead(MemToReg), .MemWrite(MemWrite));  // open: PCSrc, Branch
  Multiplexer #(.width(32)) multiplexer_1 (.in0(rd2), .in1(Imm), .out(ALU_Data), .sel(ALUSrc));
  ULA ula_1 (.src1(rd1), .src2(ALU_Data), .ALUOperation(ALUOP), .result(data), .ALUZero(ALUZero));
  Shifter #(.width(32)) shifter_1 (.in(Imm), .\dist (5'b00001));  // open: out
  Multiplexer #(.width(32)) multiplexer_2 (.in0(data), .in1(MemData), .out(RegData), .sel(MemToReg));
  DM dm_1 (
    .Address(data), .WriteEnable(MemWrite), .MemRead(MemRead), .CLK(CLK), .funct3(funct3), .WriteData(rd2),
    .ReadData(MemData));

  // Other names for the same wires on the sheet: RST = in_1

  // Notes on the sheet:
  //   2° entrada da ULA
  //   Write Back, se e saida da ULA ou memoria
endmodule

module InstructionF (
  input  CLK,
  input  RST,
  input  [7:0] NextPC,
  output [7:0] CurrentPC,
  output [31:0] Instrucao
);

  Register PC (.D(NextPC), .en(1'b1), .clk(CLK), .Q(CurrentPC), .clr(RST));
  // ROM #(.line("quad")) rom_1: pin names not known; wires that end beside it: CurrentPC

  // Notes on the sheet:
  //   contents of rom_1 (hex, n*v repeats v):
  //   93 0 50 0 13 1 70 0 93 2 0 0 b3 8 20 0 33 2 11 40 23 a0 32 0 23 a2 42 0 33 f 2 0 b3 e 2 0 63 86 10 0
  //   93 1 30 6 13 3 10 0 3 a4 2 0 83 a4 42 0 6f 5 80 0 93 1 30 6 93 5 10
  //   Memoria de instrucoes
endmodule

module IntructionD (
  input  [31:0] Instrucao,
  output [6:0] opcode,
  output [4:0] rd,
  output [2:0] funct3,
  output [4:0] rs1,
  output [4:0] rs2,
  output [6:0] funct7,
  output [11:0] I_Imm,
  output [11:0] S_Imm,
  output [11:0] B_Imm,
  output [19:0] U_Imm,
  output [19:0] J_Imm
);


  assign B_Imm = {Instrucao[25], Instrucao[7], Instrucao[31:26], Instrucao[11:8]};
  assign funct3 = Instrucao[14:12];
  assign funct7 = Instrucao[31:25];
  assign I_Imm = Instrucao[31:20];
  assign J_Imm = {Instrucao[31], Instrucao[21:12], Instrucao[22], Instrucao[30:23]};
  assign opcode = Instrucao[6:0];
  assign rd = Instrucao[11:7];
  assign rs1 = Instrucao[19:15];
  assign rs2 = Instrucao[24:20];
  assign S_Imm = {Instrucao[31:25], Instrucao[11:7]};
  assign U_Imm = Instrucao[31:12];

  // Other names for the same wires on the sheet: b4_1[3:0] = Instrucao[11:8]; b10_5[5:0] = Instrucao[31:26];
  //   b19_12[7:0] = Instrucao[30:23]; b20 = Instrucao[31]; b11 = Instrucao[7]; b12 = Instrucao[25];
  //   b10_1[9:0] = Instrucao[21:12]; b11_J = Instrucao[22]

  // Notes on the sheet:
  //   Imediato Tipo U
  //   Imediato Tipo J
  //   Imediato Tipo I
  //   Imediato Tipo S
  //   Imediato Tipo B
endmodule

module BR (
  input  CLK,
  input  RST,
  input  RegWrite,
  input  [4:0] RS1,
  input  [4:0] RS2,
  input  [4:0] RD,
  input  [31:0] Data,
  output [31:0] RD1,
  output [31:0] RD2
);

  wire WE_X1, WE_X2, WE_X3, WE_X4, WE_X5, WE_X6, WE_X7, WE_X8, WE_X9, WE_X10, WE_X11, WE_X12, WE_X13, WE_X14,
       WE_X15, WE_X16, WE_X17, WE_X18, WE_X19, WE_X20, WE_X21, WE_X22, WE_X23, WE_X24, WE_X25, WE_X26,
       WE_X27, WE_X28, WE_X29, WE_X30, WE_X31;
  wire [31:0] Q_X, Q_X1, Q_X2, Q_X3, Q_X4, Q_X5, Q_X6, Q_X7, Q_X8, Q_X9, Q_X10, Q_X11, Q_X12, Q_X13, Q_X14,
       Q_X15, Q_X16, Q_X17, Q_X18, Q_X19, Q_X20, Q_X21, Q_X22, Q_X23, Q_X24, Q_X25, Q_X26, Q_X27, Q_X28,
       Q_X29, Q_X30, Q_X31;

  Demultiplexer #(.select(5)) demultiplexer_1 (
    .out1(WE_X1), .out2(WE_X2), .out3(WE_X3), .out4(WE_X4), .out5(WE_X5), .out6(WE_X6), .out7(WE_X7),
    .out8(WE_X8), .out9(WE_X9), .out10(WE_X10), .out11(WE_X11), .out12(WE_X12), .out13(WE_X13),
    .out14(WE_X14), .out15(WE_X15), .out16(WE_X16), .out17(WE_X17), .out18(WE_X18), .out19(WE_X19),
    .out20(WE_X20), .out21(WE_X21), .out22(WE_X22), .out23(WE_X23), .out24(WE_X24), .out25(WE_X25),
    .out26(WE_X26), .out27(WE_X27), .out28(WE_X28), .out29(WE_X29), .out30(WE_X30), .out31(WE_X31),
    .in(RegWrite), .sel(RD));  // open: out0
  Register #(.trigger("falling"), .width(32)) x0 (.D({32{1'b0}}), .clk(CLK), .Q(Q_X), .clr(RST));  // open: en
  Register #(.trigger("falling"), .width(32)) x4 (.D(Data), .en(WE_X4), .clk(CLK), .Q(Q_X4), .clr(RST));
  Register #(.trigger("falling"), .width(32)) x8 (.D(Data), .en(WE_X8), .clk(CLK), .Q(Q_X8), .clr(RST));
  Register #(.trigger("falling"), .width(32)) x12 (.D(Data), .en(WE_X12), .clk(CLK), .Q(Q_X12), .clr(RST));
  Register #(.trigger("falling"), .width(32)) x16 (.D(Data), .en(WE_X16), .clk(CLK), .Q(Q_X16), .clr(RST));
  Register #(.trigger("falling"), .width(32)) x20 (.D(Data), .en(WE_X20), .clk(CLK), .Q(Q_X20), .clr(RST));
  Register #(.trigger("falling"), .width(32)) x24 (.D(Data), .en(WE_X24), .clk(CLK), .Q(Q_X24), .clr(RST));
  Register #(.trigger("falling"), .width(32)) x28 (.D(Data), .en(WE_X28), .clk(CLK), .Q(Q_X28), .clr(RST));
  Register #(.trigger("falling"), .width(32)) x1 (.D(Data), .en(WE_X1), .clk(CLK), .Q(Q_X1), .clr(RST));
  Register #(.trigger("falling"), .width(32)) x5 (.D(Data), .en(WE_X5), .clk(CLK), .Q(Q_X5), .clr(RST));
  Register #(.trigger("falling"), .width(32)) x9 (.D(Data), .en(WE_X9), .clk(CLK), .Q(Q_X9), .clr(RST));
  Register #(.trigger("falling"), .width(32)) x13 (.D(Data), .en(WE_X13), .clk(CLK), .Q(Q_X13), .clr(RST));
  Register #(.trigger("falling"), .width(32)) x17 (.D(Data), .en(WE_X17), .clk(CLK), .Q(Q_X17), .clr(RST));
  Register #(.trigger("falling"), .width(32)) x21 (.D(Data), .en(WE_X21), .clk(CLK), .Q(Q_X21), .clr(RST));
  Register #(.trigger("falling"), .width(32)) x25 (.D(Data), .en(WE_X25), .clk(CLK), .Q(Q_X25), .clr(RST));
  Register #(.trigger("falling"), .width(32)) x29 (.D(Data), .en(WE_X29), .clk(CLK), .Q(Q_X29), .clr(RST));
  Register #(.trigger("falling"), .width(32)) x2 (.D(Data), .en(WE_X2), .clk(CLK), .Q(Q_X2), .clr(RST));
  Register #(.trigger("falling"), .width(32)) x6 (.D(Data), .en(WE_X6), .clk(CLK), .Q(Q_X6), .clr(RST));
  Register #(.trigger("falling"), .width(32)) x10 (.D(Data), .en(WE_X10), .clk(CLK), .Q(Q_X10), .clr(RST));
  Register #(.trigger("falling"), .width(32)) x14 (.D(Data), .en(WE_X14), .clk(CLK), .Q(Q_X14), .clr(RST));
  Register #(.trigger("falling"), .width(32)) x18 (.D(Data), .en(WE_X18), .clk(CLK), .Q(Q_X18), .clr(RST));
  Register #(.trigger("falling"), .width(32)) x22 (.D(Data), .en(WE_X22), .clk(CLK), .Q(Q_X22), .clr(RST));
  Register #(.trigger("falling"), .width(32)) x26 (.D(Data), .en(WE_X26), .clk(CLK), .Q(Q_X26), .clr(RST));
  Register #(.trigger("falling"), .width(32)) x30 (.D(Data), .en(WE_X30), .clk(CLK), .Q(Q_X30), .clr(RST));
  Register #(.trigger("falling"), .width(32)) x3 (.D(Data), .en(WE_X3), .clk(CLK), .Q(Q_X3), .clr(RST));
  Register #(.trigger("falling"), .width(32)) x7 (.D(Data), .en(WE_X7), .clk(CLK), .Q(Q_X7), .clr(RST));
  Register #(.trigger("falling"), .width(32)) x11 (.D(Data), .en(WE_X11), .clk(CLK), .Q(Q_X11), .clr(RST));
  Register #(.trigger("falling"), .width(32)) x15 (.D(Data), .en(WE_X15), .clk(CLK), .Q(Q_X15), .clr(RST));
  Register #(.trigger("falling"), .width(32)) x19 (.D(Data), .en(WE_X19), .clk(CLK), .Q(Q_X19), .clr(RST));
  Register #(.trigger("falling"), .width(32)) x23 (.D(Data), .en(WE_X23), .clk(CLK), .Q(Q_X23), .clr(RST));
  Register #(.trigger("falling"), .width(32)) x27 (.D(Data), .en(WE_X27), .clk(CLK), .Q(Q_X27), .clr(RST));
  Register #(.trigger("falling"), .width(32)) x31 (.D(Data), .en(WE_X31), .clk(CLK), .Q(Q_X31), .clr(RST));
  Multiplexer #(.select(5), .width(32)) multiplexer_1 (
    .in0(Q_X), .in1(Q_X1), .in2(Q_X2), .in3(Q_X3), .in4(Q_X4), .in5(Q_X5), .in6(Q_X6), .in7(Q_X7),
    .in8(Q_X8), .in9(Q_X9), .in10(Q_X10), .in11(Q_X11), .in12(Q_X12), .in13(Q_X13), .in14(Q_X14),
    .in15(Q_X15), .in16(Q_X16), .in17(Q_X17), .in18(Q_X18), .in19(Q_X19), .in20(Q_X20), .in21(Q_X21),
    .in22(Q_X22), .in23(Q_X23), .in24(Q_X24), .in25(Q_X25), .in26(Q_X26), .in27(Q_X27), .in28(Q_X28),
    .in29(Q_X29), .in30(Q_X30), .in31(Q_X31), .out(RD1), .sel(RS1));
  Multiplexer #(.select(5), .width(32)) multiplexer_2 (
    .in0(Q_X), .in1(Q_X1), .in2(Q_X2), .in3(Q_X3), .in4(Q_X4), .in5(Q_X5), .in6(Q_X6), .in7(Q_X7),
    .in8(Q_X8), .in9(Q_X9), .in10(Q_X10), .in11(Q_X11), .in12(Q_X12), .in13(Q_X13), .in14(Q_X14),
    .in15(Q_X15), .in16(Q_X16), .in17(Q_X17), .in18(Q_X18), .in19(Q_X19), .in20(Q_X20), .in21(Q_X21),
    .in22(Q_X22), .in23(Q_X23), .in24(Q_X24), .in25(Q_X25), .in26(Q_X26), .in27(Q_X27), .in28(Q_X28),
    .in29(Q_X29), .in30(Q_X30), .in31(Q_X31), .out(RD2), .sel(RS2));

  // Other names for the same wires on the sheet: RW = RegWrite
endmodule

module ULA (
  input  [31:0] src1,
  input  [31:0] src2,
  input  [3:0] ALUOperation,
  output [31:0] result,
  output ALUZero
);

  wire comparator_1_eq, comparator_1_gt, comparator_1_lt, comparator_2_eq, comparator_2_gt, comparator_2_lt,
       comparator_3_eq, not_1_out, or_2_out, or_3_out;
  wire [31:0] add, and_logic, beq, bge, bgeu, bne, or_logic, shiftL_logic, shiftR_logic, shiftRA_logic,
       slt_logic, sltu_logic, sub, xor_logic;

  Adder #(.width(32)) adder_1 (.a(src1), .b(src2), .out(add));  // open: cin, cout
  Subtractor #(.width(32)) subtractor_1 (.a(src1), .b(src2), .out(sub));  // open: bin, bout
  assign xor_logic = src1 ^ src2;  // XOR_Gate xor_1, 32 bits wide
  assign or_logic = src1 | src2;  // OR_Gate or_1, 32 bits wide
  assign and_logic = src1 & src2;  // AND_Gate and_1, 32 bits wide
  Shifter #(.width(32)) shifter_1 (.in(src1), .\dist (src2[4:0]), .out(shiftL_logic));
  Shifter #(.shift("lr"), .width(32)) shifter_2 (.in(src1), .\dist (src2[4:0]), .out(shiftR_logic));
  Shifter #(.shift("ar"), .width(32)) shifter_3 (.in(src1), .\dist (src2[4:0]), .out(shiftRA_logic));
  Comparator #(.width(32)) comparator_1 (
    .a(src1), .b(src2), .gt(comparator_1_gt), .eq(comparator_1_eq), .lt(comparator_1_lt));
  Comparator #(.mode("unsigned"), .width(32)) comparator_2 (
    .a(src1), .b(src2), .gt(comparator_2_gt), .eq(comparator_2_eq), .lt(comparator_2_lt));
  assign slt_logic = {{31{1'b0}}, comparator_1_lt};  // Bit_Extender bit_extender_1
  or or_2 (or_2_out, comparator_2_gt, comparator_2_eq);
  assign sltu_logic = {{31{1'b0}}, comparator_2_lt};  // Bit_Extender bit_extender_2
  assign bge = {{31{1'b0}}, or_3_out};  // Bit_Extender bit_extender_3
  or or_3 (or_3_out, comparator_1_gt, comparator_1_eq);
  assign bne = {{31{1'b0}}, not_1_out};  // Bit_Extender bit_extender_4
  not not_1 (not_1_out, comparator_1_eq);
  assign bgeu = {{31{1'b0}}, or_2_out};  // Bit_Extender bit_extender_5
  assign beq = {{31{1'b0}}, comparator_2_eq};  // Bit_Extender bit_extender_6
  Multiplexer #(.select(4), .width(32)) multiplexer_1 (
    .in0(add), .in1(sub), .in2(shiftL_logic), .in3(beq), .in4(slt_logic), .in5(bne), .in6(sltu_logic),
    .in7(bgeu), .in8(xor_logic), .in9(bge), .in10(slt_logic), .in11(shiftRA_logic), .in12(or_logic),
    .in14(and_logic), .out(result), .sel(ALUOperation));  // open: in13, in15
  // Probe on result
  Comparator #(.width(32)) comparator_3 (.a({32{1'b0}}), .b(result), .eq(comparator_3_eq));  // open: gt, lt
  not not_2 (ALUZero, comparator_3_eq);

  // Other names for the same wires on the sheet: ALUOp[3:0] = ALUOperation

  // Notes on the sheet:
  //   Or
  //   And
  //   Shift left
  //   Shift right
  //   Add
  //   Sub
  //   Xor
  //   Shift right aritmetic
  //   Set last than
  //   Set last than unsigned
endmodule

module ImmGen (
  input  [2:0] ImmSel,
  input  [11:0] I_imm,
  input  [11:0] S_imm,
  input  [11:0] B_imm,
  input  [19:0] U_imm,
  input  [19:0] J_imm,
  output [31:0] Imediato
);

  wire [31:0] B_32b, I_32b, J_32b, S_32b;

  assign J_32b = {{11{J_imm[19]}}, {J_imm, 1'b0}};  // Bit_Extender bit_extender_1
  assign I_32b = {{20{I_imm[11]}}, I_imm};  // Bit_Extender bit_extender_2
  assign S_32b = {{20{S_imm[11]}}, S_imm};  // Bit_Extender bit_extender_3
  assign B_32b = {{19{B_imm[11]}}, {B_imm, 1'b0}};  // Bit_Extender bit_extender_4
  Multiplexer #(.select(3), .width(32)) multiplexer_1 (
    .in0(I_32b), .in1(S_32b), .in2(B_32b), .in3({U_imm, {12{1'b0}}}), .in4(J_32b), .out(Imediato),
    .sel(ImmSel));  // open: in5, in6, in7

  // Other names for the same wires on the sheet: Imm[31:0] = Imediato; U_32b[31:12] = U_imm

  // Notes on the sheet:
  //   Instrucao tipo I
  //   Instrucao tipo S
  //   Instrucao tipo B
  //   Instrucao tipo U
  //   Instrucao tipo J
endmodule

module UC (
  input  [6:0] opcode,
  input  [2:0] funct3,
  input  [6:0] funct7,
  input  CLK,
  output [2:0] ImmSel,
  output RegWrite,
  output ALUSrc,
  output PCSrc,
  output [3:0] ALUOp,
  output Branch,
  output MemRead,
  output MemToRead,
  output MemWrite
);

  wire is_I, is_U, Tipo_I_AR, Tipo_I_Jarl, Tipo_I_Load, Tipo_R, Tipo_U_AUIPC, Tipo_U_LUI;
  wire [0:0] Sel_ALUOp;
  wire [3:0] ALUOp_Branch;

  Decoder #(.select(7)) decoder_1 (
    .out3(Tipo_I_Load), .out19(Tipo_I_AR), .out23(Tipo_U_AUIPC), .out35(MemWrite), .out51(Tipo_R),
    .out55(Tipo_U_LUI), .out99(Branch), .out103(Tipo_I_Jarl), .out111(ImmSel[2]), .sel(opcode), .en(CLK));  // open: out0, out1, out2, out4, out5, out6, out7, out8, out9, out10, out11, out12, out13, out14, out15, out16, out17, out18, out20, out21, out22, out24, out25, out26, out27, out28, out29, out30, out31, out32, out33, out34, out36, out37, out38, out39, out40, out41, out42, out43, out44, out45, out46, out47, out48, out49, out50, out52, out53, out54, out56, out57, out58, out59, out60, out61, out62, out63, out64, out65, out66, out67, out68, out69, out70, out71, out72, out73, out74, out75, out76, out77, out78, out79, out80, out81, out82, out83, out84, out85, out86, out87, out88, out89, out90, out91, out92, out93, out94, out95, out96, out97, out98, out100, out101, out102, out104, out105, out106, out107, out108, out109, out110, out112, out113, out114, out115, out116, out117, out118, out119, out120, out121, out122, out123, out124, out125, out126, out127
  or or_1 (ImmSel[0], MemWrite, is_U);
  Multiplexer #(.select(3), .width(4)) multiplexer_1 (
    .in0(4'b0011), .in1(4'b0101), .in4(4'b0100), .in5(4'b1001), .in6(4'b0110), .in7(4'b0111),
    .out(ALUOp_Branch), .sel(funct3));  // open: in2, in3
  or or_2 (is_U, Tipo_U_LUI, Tipo_U_AUIPC);
  // Probe on {ImmSel[2], Branch, ImmSel[0]}
  or or_3 (Sel_ALUOp[0], Tipo_I_AR, Tipo_R);
  // Probe on ALUOp
  Multiplexer #(.select(2), .width(4)) multiplexer_2 (
    .in0(4'b0000), .in1({funct3, funct7[5]}), .in2(ALUOp_Branch), .out(ALUOp), .sel({Branch, Sel_ALUOp[0]}));  // open: in3
  // Probe on {Branch, Sel_ALUOp[0]}
  or or_4 (ALUSrc, MemWrite, is_I);
  or or_5 (is_I, Tipo_I_Load, Tipo_I_AR, Tipo_I_Jarl);
  or or_6 (PCSrc, ImmSel[2], Tipo_U_AUIPC, Tipo_I_Jarl);
  or or_7 (MemRead, Tipo_I_Load, Tipo_U_LUI);
  or or_8 (RegWrite, is_I, is_U, Tipo_R);

  assign ImmSel[1] = Branch;
  assign MemToRead = MemRead;

  // Other names for the same wires on the sheet: ALUOp_AR[3:0] = {funct3, funct7[5]}; funct7_b5 = funct7[5];
  //   Tipo_J = ImmSel[2]; Sel_ALUOp[1] = Branch; Tipo_B = Branch; Tipo_S = MemWrite

  // Notes on the sheet:
  //   ALUOp Aritmetico
  //   ALUSrc
  //   MemRead
  //   PCSrc
  //   RegWrite
endmodule

module DM (
  input  [31:0] Address,
  input  WriteEnable,
  input  MemRead,
  input  CLK,
  input  [2:0] funct3,
  input  [31:0] WriteData,
  output [31:0] ReadData
);

  wire [7:0] load_b1, load_b2, load_b3, load_b4;
  wire [31:0] load_BU, load_byte, load_half, load_hwu, ram_1_dout, StoreByte, StoreData, StoreHalfWord;

  // Probe on WriteData[7:0]
  assign StoreHalfWord = {{16{1'b0}}, {WriteData[7:0], WriteData[15:8]}};  // Bit_Extender bit_extender_1
  assign StoreByte = {{24{1'b0}}, WriteData[7:0]};  // Bit_Extender bit_extender_2
  Multiplexer #(.select(3), .width(32)) multiplexer_1 (
    .in0(StoreByte), .in1(StoreHalfWord),
    .in2({WriteData[7:0], WriteData[15:8], WriteData[23:16], WriteData[31:24]}), .out(StoreData), .sel(funct3));  // open: in3, in4, in5, in6, in7
  RAM #(.addrWidth(12), .asyncread("true"), .dataWidth(32)) ram_1 (
    .addr(Address[11:0]), .we(WriteEnable), .oe(MemRead), .clk(CLK), .din(StoreData), .dout(ram_1_dout));
  // Probe on {load_b4, load_b3, load_b2, load_b1}
  assign {load_b4, load_b3, load_b2, load_b1} = MemRead ? ram_1_dout : 32'bz;  // Controlled_Buffer controlled_buffer_1
  assign load_half = {{16{load_b3[7]}}, {load_b3, load_b4}};  // Bit_Extender bit_extender_3
  assign load_hwu = {{16{1'b0}}, {load_b3, load_b4}};  // Bit_Extender bit_extender_4
  assign load_byte = {{24{load_b4[7]}}, load_b4};  // Bit_Extender bit_extender_5
  assign load_BU = {{24{1'b0}}, load_b4};  // Bit_Extender bit_extender_6
  // Probe on {load_b1, load_b2, load_b3, load_b4}
  Multiplexer #(.select(3), .width(32)) multiplexer_2 (
    .in0(load_byte), .in1(load_half), .in2({load_b1, load_b2, load_b3, load_b4}), .in4(load_BU),
    .in5(load_hwu), .out(ReadData), .sel(funct3));  // open: in3, in6, in7

  // Other names for the same wires on the sheet: store_b2[7:0] = WriteData[15:8];
  //   StoreWord[31:0] = {WriteData[7:0], WriteData[15:8], WriteData[23:16], WriteData[31:24]};
  //   store_b1[7:0] = WriteData[7:0]; load_word[31:0] = {load_b1, load_b2, load_b3, load_b4}; ME = MemRead;
  //   store_b4[7:0] = WriteData[31:24]; store_b3[7:0] = WriteData[23:16]; WE = WriteEnable

  // Notes on the sheet:
  //   Load Word
  //   Load Half Word
  //   Load Half Word Unsigned
  //   Load Byte
  //   Load Byte Unsigned
endmodule
