// Logisim project projetopentregar.circ as structural Verilog: 8 circuits, main circuit main
module main (
  input  RST
);

  wire ALUSrc, ALUZero, and_1_out, and_2_out, Branch, CLK, Jump, MemRead, MemToRead, MemWrite, RegWrite, SW;
  wire [1:0] OffSel;
  wire [2:0] ALUOp, funct, rd, rs1_banco, rs2_banco;
  wire [3:0] opcode;
  wire [5:0] B_offset, I_imm, S_offset;
  wire [8:0] J_offset;
  wire [15:0] ALU_Data, BRData, CurrentPC, data, DataOut, instrucao, Jump1, NextPC, OffsetSel, PC1,
       PC_Branch, PCJump, rd1, rd2, WB_Regular, WriteDataBR;

  // Probe on NextPC
  Multiplexer #(.width(16)) multiplexer_1 (.in0(rd2), .in1(OffsetSel), .out(ALU_Data), .sel(ALUSrc));
  // Probe on OffsetSel
  // Probe on PC1
  // Probe on OffsetSel
  Multiplexer #(.width(16)) multiplexer_2 (.in0(data), .in1(DataOut), .out(WB_Regular), .sel(MemToRead));
  Multiplexer #(.width(16)) multiplexer_3 (.in0(WB_Regular), .in1(PC1), .out(WriteDataBR), .sel(Jump));
  // Probe on ALU_Data
  // Probe on PCJump
  Adder #(.width(16)) adder_1 (.a(PC1), .b(OffsetSel), .out(PCJump));  // open: cin, cout
  // Probe on WriteDataBR
  Adder #(.width(16)) adder_2 (.a(16'h1), .b(CurrentPC), .out(PC1));  // open: cin, cout
  // Probe on data
  // Probe on CurrentPC
  IntructionF intructionf_1 (.RST(RST), .NextPC(NextPC), .CLK(CLK), .CurrentPC(CurrentPC), .Instrucao(instrucao));
  // Probe on BRData
  Multiplexer #(.width(16)) multiplexer_4 (.in0(data), .in1(DataOut), .out(BRData), .sel(MemToRead));
  Multiplexer #(.width(16)) multiplexer_5 (.in0(PC1), .in1(PC_Branch), .out(Jump1), .sel(and_1_out));
  and and_1 (and_1_out, Branch, ALUZero);
  // Probe on PC_Branch
  // Probe on instrucao
  Multiplexer #(.width(16)) multiplexer_6 (.in0(PC1), .in1(PC_Branch), .out(Jump1), .sel(and_2_out));
  and and_2 (and_2_out, Branch, ALUZero);
  // Probe on Jump1
  Clock u_CLK (.out(CLK));
  Multiplexer #(.width(16)) multiplexer_7 (.in0(Jump1), .in1(PCJump), .out(NextPC), .sel(Jump));
  // Probe on PC1
  InstuctionD instuctiond_1 (
    .Instrucao(instrucao), .SW(SW), .funct(funct), .rs1(rs1_banco), .rs2(rs2_banco), .rd(rd),
    .opcode(opcode), .I_imm(I_imm), .S_offset(S_offset), .B_offset(B_offset), .J_offset(J_offset));
  // Probe on PC_Branch
  Adder #(.width(16)) adder_3 (.a(PC1), .b(OffsetSel), .out(PC_Branch));  // open: cin, cout
  // Probe on WriteDataBR
  UC uc_1 (
    .opcode(opcode), .funct(funct), .CLK(CLK), .RegWrite(RegWrite), .ALUSrc(ALUSrc), .Branch(Branch),
    .MemWrite(MemWrite), .Jump(Jump), .MemRead(MemRead), .MemToRead(MemToRead), .ALUOp(ALUOp),
    .OffSel(OffSel), .SW(SW));
  // Probe on rd1
  BR br_1 (
    .CLK(CLK), .RST(RST), .RegWrite(RegWrite), .RS1(rs1_banco), .RS2(rs2_banco), .RD(rd), .Data(WriteDataBR),
    .rd1(rd1), .rd2(rd2));
  // Probe on rd2
  // Probe on OffsetSel
  ImmGen immgen_1 (
    .OffSel(OffSel), .I_Imm(I_imm), .S_Offset(S_offset), .B_Offset(B_offset), .J_Offset(J_offset),
    .Offset_Imm(OffsetSel));
  // Probe on ALU_Data
  // Probe on data
  // Probe on rd1
  ULA ula_1 (.src1(rd1), .src2(ALU_Data), .ALUOperation(ALUOp), .Result(data), .ALUZero(ALUZero));
  // Probe on DataOut
  DM dm_1 (.WriteEnable(MemWrite), .MemRead(MemRead), .Address(data), .CLK(CLK), .WriteData(rd2), .DataOut(DataOut));
  // Probe on data

  // Notes on the sheet:
  //   2° Entrada da ULA
  //   Jump
  //   WriteBack BR
  //   Branch
endmodule

module IntructionF (
  input  RST,
  input  [15:0] NextPC,
  input  CLK,
  output [15:0] CurrentPC,
  output [15:0] Instrucao
);

  // Probe on NextPC
  Register #(.width(16)) PC (.D(NextPC), .en(1'b1), .clk(CLK), .Q(CurrentPC), .clr(RST));
  ROM #(.addrWidth(10), .dataWidth(16)) rom_1 (.addr(CurrentPC[9:0]), .data(Instrucao));

  // Notes on the sheet:
  //   contents of rom_1 (hex, n*v repeats v):
  //   0 1202 3050 121f 125d 3051 1203 3052 121e 3053 2210 2411 2612 2813 a5c 4a0f d14 4c07 1e02 1c1f 1d81
  //   3dc0 3dc1 600c 1e01 1c1f 1d81 3dc0 3dc1 6005 1e00 1c1f 1d81 3dc0 3dc1 6000
  //   Memoria de instrucoes
endmodule

module InstuctionD (
  input  [15:0] Instrucao,
  input  SW,
  output [2:0] funct,
  output [2:0] rs1,
  output [2:0] rs2,
  output [2:0] rd,
  output [3:0] opcode,
  output [5:0] I_imm,
  output [5:0] S_offset,
  output [5:0] B_offset,
  output [8:0] J_offset
);

  Multiplexer #(.width(3)) multiplexer_1 (.in0(Instrucao[8:6]), .in1(Instrucao[11:9]), .out(rs1), .sel(SW));
  Multiplexer #(.width(3)) multiplexer_2 (.in0(Instrucao[5:3]), .in1(Instrucao[8:6]), .out(rs2), .sel(SW));

  assign B_offset = Instrucao[5:0];
  assign funct = Instrucao[2:0];
  assign I_imm = Instrucao[5:0];
  assign J_offset = Instrucao[8:0];
  assign opcode = Instrucao[15:12];
  assign rd = Instrucao[11:9];
  assign S_offset = Instrucao[5:0];

  // Other names for the same wires on the sheet: rs2_t[2:0] = Instrucao[5:3]; rs1_t[2:0] = Instrucao[8:6];
  //   rs1_banco[2:0] = rs1; rs2_banco[2:0] = rs2

  // Notes on the sheet:
  //   Imetiato Tipo I
  //   Offset Tipo B
  //   rs1 do SW
  //   rs2 do SW
  //   Offset Tipo S
  //   Offset Tipo J
endmodule

module BR (
  input  CLK,
  input  RST,
  input  RegWrite,
  input  [2:0] RS1,
  input  [2:0] RS2,
  input  [2:0] RD,
  input  [15:0] Data,
  output [15:0] rd1,
  output [15:0] rd2
);

  wire WE_R1, WE_R2, WE_R3, WE_R4, WE_R5, WE_R6, WE_R7;
  wire [15:0] Q_R0, Q_R1, Q_R2, Q_R3, Q_R4, Q_R5, Q_R6, Q_R7;

  Demultiplexer #(.select(3)) demultiplexer_1 (
    .out1(WE_R1), .out2(WE_R2), .out3(WE_R3), .out4(WE_R4), .out5(WE_R5), .out6(WE_R6), .out7(WE_R7),
    .in(RegWrite), .sel(RD));  // open: out0
  Register #(.trigger("falling"), .width(16)) R0 (.D({16{1'b0}}), .clk(CLK), .Q(Q_R0), .clr(RST));  // open: en
  Register #(.width(16)) R4 (.D(Data), .en(WE_R4), .clk(CLK), .Q(Q_R4), .clr(RST));
  Register #(.width(16)) R1 (.D(Data), .en(WE_R1), .clk(CLK), .Q(Q_R1), .clr(RST));
  Register #(.width(16)) R5 (.D(Data), .en(WE_R5), .clk(CLK), .Q(Q_R5), .clr(RST));
  Register #(.width(16)) R2 (.D(Data), .en(WE_R2), .clk(CLK), .Q(Q_R2), .clr(RST));
  Register #(.width(16)) R6 (.D(Data), .en(WE_R6), .clk(CLK), .Q(Q_R6), .clr(RST));
  Register #(.width(16)) R3 (.D(Data), .en(WE_R3), .clk(CLK), .Q(Q_R3), .clr(RST));
  Register #(.width(16)) R7 (.D(Data), .en(WE_R7), .clk(CLK), .Q(Q_R7), .clr(RST));
  Multiplexer #(.select(3), .width(16)) multiplexer_1 (
    .in0(Q_R0), .in1(Q_R1), .in2(Q_R2), .in3(Q_R3), .in4(Q_R4), .in5(Q_R5), .in6(Q_R6), .in7(Q_R7),
    .out(rd1), .sel(RS1));
  Multiplexer #(.select(3), .width(16)) multiplexer_2 (
    .in0(Q_R0), .in1(Q_R1), .in2(Q_R2), .in3(Q_R3), .in4(Q_R4), .in5(Q_R5), .in6(Q_R6), .in7(Q_R7),
    .out(rd2), .sel(RS2));

  // Other names for the same wires on the sheet: RW = RegWrite
endmodule

module ULA (
  input  [15:0] src1,
  input  [15:0] src2,
  input  [2:0] ALUOperation,
  output [15:0] Result,
  output ALUZero
);

  wire comparator_1_lt, or_2_out;
  wire [15:0] Add, And_Logic, Or_Logic, Slt_Logic, Sub;

  Adder #(.width(16)) adder_1 (.a(src1), .b(src2), .out(Add));  // open: cin, cout
  Subtractor #(.width(16)) subtractor_1 (.a(src1), .b(src2), .out(Sub));  // open: bin, bout
  assign And_Logic = src1 & src2;  // AND_Gate and_1, 16 bits wide
  assign Or_Logic = src1 | src2;  // OR_Gate or_1, 16 bits wide
  Comparator #(.width(16)) comparator_1 (.a(src1), .b(src2), .lt(comparator_1_lt));  // open: gt, eq
  assign Slt_Logic = {{15{1'b0}}, comparator_1_lt};  // Bit_Extender bit_extender_1
  // Probe on Result
  Multiplexer #(.select(3), .width(16)) multiplexer_1 (
    .in0(Add), .in1(Sub), .in2(And_Logic), .in3(Or_Logic), .in4(Slt_Logic), .out(Result), .sel(ALUOperation));  // open: in5, in6, in7
  or or_2 (or_2_out, Result[0], Result[1], Result[2], Result[3], Result[4], Result[5], Result[6], Result[7], Result[8], Result[9], Result[10], Result[11], Result[12], Result[13], Result[14], Result[15]);
  not not_1 (ALUZero, or_2_out);

  // Other names for the same wires on the sheet: ALUOp[2:0] = ALUOperation

  // Notes on the sheet:
  //   Add
  //   Sub
  //   And
  //   Or
  //   Set Last Than
  //   ALUOp
  //   000 - Add (0)
  //   001 - Sub (1)
  //   010 - And (2)
  //   011 - Or (3)
  //   100 - Slt (4)
endmodule

module ImmGen (
  input  [1:0] OffSel,
  input  [5:0] I_Imm,
  input  [5:0] S_Offset,
  input  [5:0] B_Offset,
  input  [8:0] J_Offset,
  output [15:0] Offset_Imm
);

  wire [15:0] B_Offset16, Imm_16, J_Offset16, S_Offset16;

  assign B_Offset16 = {{10{B_Offset[5]}}, B_Offset};  // Bit_Extender bit_extender_1
  assign J_Offset16 = {{7{J_Offset[8]}}, J_Offset};  // Bit_Extender bit_extender_2
  assign Imm_16 = {{10{I_Imm[5]}}, I_Imm};  // Bit_Extender bit_extender_3
  assign S_Offset16 = {{10{S_Offset[5]}}, S_Offset};  // Bit_Extender bit_extender_4
  Multiplexer #(.select(2), .width(16)) multiplexer_1 (
    .in0(Imm_16), .in1(S_Offset16), .in2(B_Offset16), .in3(J_Offset16), .out(Offset_Imm), .sel(OffSel));

  // Notes on the sheet:
  //   Instrucao tipo I
  //   Offset tipo S
  //   Offset tipo B
  //   Offset tipo J
endmodule

module UC (
  input  [3:0] opcode,
  input  [2:0] funct,
  input  CLK,
  output RegWrite,
  output ALUSrc,
  output Branch,
  output MemWrite,
  output Jump,
  output MemRead,
  output MemToRead,
  output [2:0] ALUOp,
  output [1:0] OffSel,
  output SW
);

  wire add, addf, and_f, and_logic, Beq, Bne, I_AR, is_I, or_f, or_logic, R_Type, slt_f, sub, subf;

  Decoder #(.select(4)) decoder_1 (
    .out0(R_Type), .out1(I_AR), .out2(MemRead), .out3(MemWrite), .out4(Beq), .out5(Bne), .out6(Jump),
    .sel(opcode), .en(1'b1));  // open: out7, out8, out9, out10, out11, out12, out13, out14, out15
  or or_1 (OffSel[0], Branch, Jump);
  or or_2 (OffSel[1], MemWrite, Jump);
  Decoder #(.select(3)) decoder_2 (
    .out0(addf), .out1(subf), .out2(and_f), .out3(or_f), .out4(slt_f), .sel(funct), .en(1'b1));  // open: out5, out6, out7
  and and_1 (add, R_Type, addf);
  and and_2 (sub, R_Type, subf);
  and and_3 (and_logic, R_Type, and_f);
  and and_4 (or_logic, R_Type, or_f);
  or or_3 (is_I, I_AR, MemRead);
  or or_4 (RegWrite, is_I, Jump, R_Type);
  and and_5 (ALUOp[2], R_Type, slt_f);
  or or_5 (ALUSrc, I_AR, MemRead, MemWrite);
  or or_6 (ALUOp[0], sub, or_logic, Branch);
  or or_7 (ALUOp[1], and_logic, or_logic);
  or or_8 (Branch, Beq, Bne);

  assign MemToRead = MemRead;
  assign SW = MemWrite;

  // Other names for the same wires on the sheet: slt_logic = ALUOp[2]; I_Load = MemRead; Jal = Jump;
  //   offsel11 = OffSel[0]; offsel10 = OffSel[1]

  // Notes on the sheet:
  //   Instrucao
  //   add/lw
  //   sw
  //   beq/bne
  //   jal
  //   OffSel
  //   0
  //   0
  //   1
  //   1
  //   offsel11
  //   0
  //   1
  //   0
  //   1
  //   offsel10
  //   01
  //   10
  //   OffSel
  //   00
  //   11
  //   ALUOp
  //   RegWrite
  //   ALUSrc
  //   Branch
endmodule

module DM (
  input  WriteEnable,
  input  MemRead,
  input  [15:0] Address,
  input  CLK,
  input  [15:0] WriteData,
  output [15:0] DataOut
);

  // Probe on WriteData
  RAM #(.addrWidth(6), .dataWidth(16)) ram_1 (
    .addr(Address[5:0]), .we(WriteEnable), .oe(MemRead), .clk(CLK), .din(WriteData), .dout(DataOut));
  // Probe on DataOut

  // Other names for the same wires on the sheet: MemWrite = WriteEnable; rd2[15:0] = WriteData

  // Notes on the sheet:
  //   Endereço
  //   0x10
  //   0x11
  //   0x12
  //   0x13
  //   Endereço
  //   0x20
  //   0x21
  //   0x10
  //   0x11
  //   0x12
  //   0x13
  //   0x20
  //   0x21
  //   Entrada
  //   Saída
  //   Caso 1 - Emergência
  //   0002
  //   003C
  //   0003
  //   001E
  //   Saída
  //   0002
  //   0002
  //   Nome
  //   DIST_ATUAL
  //   VEL_ATUAL
  //   DIST_SEGURA
  //   VEL_MAX
  //   Nome
  //   CMD_FREIO
  //   STATUS
  //   0x10
  //   0x11
  //   0x12
  //   0x13
  //   0x20
  //   0x21
  //   Caso 2 - Normal
  //   0032     # 50
  //   0028     # 40
  //   0003
  //   003C     # 60
  //   Saída
  //   0000
  //   0000
  //   Caso 3 - Alerta
  //   0x10
  //   0x11
  //   0x12
  //   0x13
  //   Saída
  //   0x20
  //   0x21
  //   0002
  //   0014     # 20
  //   0003
  //   001E     # 30
  //   0001
  //   0001
  //   Caso 4 - Limite Exato
  //   0x10
  //   0x11
  //   0x12
  //   0x13
  //   Saída
  //   0x20
  //   0x21
  //   0003
  //   001E     # 30
  //   0003
  //   0028     # 40
  //   0000
  //   0000
  //   Caso 4 - Alta Vel. Distância Seg.
  //   0x10
  //   0x11
  //   0003
  //   0x12
  //   0x13
  //   Saída
  //   0x20
  //   0x21
  //   001E      # 30
  //   0050      # 80
  //   0032      # 50
  //   0000
  //   0000
endmodule
